# Fritzing sketch Proyecto-1 ard (2) (saved by Fritzing 0.9.3b)
circuit board: 10.5708cm x 5.62579cm

parts:
  KY-1 = Keyes Relay [package=THT]
  Parte2 = Arduino Mega ADK (Rev3)
  Parte1 = Bluetooth HC-05 Macho

nets:
  N1: KY-1.signal, Parte2.D2_PWM
  5V: KY-1.power, Parte2.5V, Parte1.VCC
  GND: KY-1.ground, Parte2.GND, Parte1.GND
  N2: Parte2.D0/RX0, Parte1.TXD
  N3: Parte2.D1/TX0, Parte1.RXD

notes:
  Arduino-1, 1

custom parts:
  Keyes Relay: The Keyes 5V relay module is suitable for SCM development, home appliance control. It uses a 5V~12V TIL control signal which can control DC / AC signal.

// code stored in the sketch: Untitled.ino
int 2;

void setup{

}
void loop{
}
